// Logisim project lel112_proj2.circ as structural Verilog: 6 circuits, main circuit main
module main (
);

  wire ALUbsrc, beq, bge, blt, bne, Branch, BranchWorks, CLK, clock_1_out, comparator_2_eq, comparator_2_gt,
       comparator_3_gt, comparator_3_lt, Display_WE, halt, Jselect, jump, Mem_WE, multiplexer_1_out, Reg_WE,
       tick_out;
  wire [1:0] BranchOP;
  wire [2:0] alu_op, rd, RegDataSrc, rs, rt;
  wire [3:0] display_1_digit0, display_1_digit1, display_1_digit2, display_1_digit3;
  wire [7:0] pc_fsm_1_pc_out;
  wire [15:0] ALU_out, imm, imm__8, multiplexer_2_out, multiplexer_3_out, multiplexer_4_out, PC_1, Ram_Data,
       REG_rs, REG_rt;
  wire [21:0] rom_1_data;

  Clock clock_1 (.out(clock_1_out));
  Button tick (.out(tick_out));
  or or_1 (CLK, clock_1_out, tick_out);
  Bit_Extender #(.in_width(16), .out_width(4)) bit_extender_1 ();  // open: in, out
  Multiplexer #(.select(2)) multiplexer_1 (
    .in0(blt), .in1(bge), .in2(beq), .in3(bne), .out(multiplexer_1_out), .sel(BranchOP));  // open: en
  Shifter #(.width(16)) shifter_1 (.in(imm), .\dist (4'b1000), .out(imm__8));
  Multiplexer #(.width(16)) multiplexer_2 (
    .in0(REG_rs), .in1(imm), .out(multiplexer_2_out), .sel(Jselect));  // open: en
  and and_1 (BranchWorks, multiplexer_1_out, Branch);
  Comparator #(.width(16)) comparator_1 (.a(REG_rs), .b(REG_rt), .eq(beq), .lt(blt));  // open: gt
  Comparator #(.width(16)) comparator_2 (
    .a(REG_rs), .b(REG_rt), .gt(comparator_2_gt), .eq(comparator_2_eq));  // open: lt
  Comparator #(.width(16)) comparator_3 (
    .a(REG_rs), .b(REG_rt), .gt(comparator_3_gt), .lt(comparator_3_lt));  // open: eq
  PC_FSM pc_fsm_1 (
    .CLK(CLK), .offset(imm), .target(multiplexer_2_out), .Jump(jump), .Branch(BranchWorks), .Halt(halt),
    .PC_Out(pc_fsm_1_pc_out), .PC_1_Out(PC_1));
  // Probe on pc_fsm_1_pc_out
  or or_2 (bge, comparator_2_gt, comparator_2_eq);
  or or_3 (bne, comparator_3_gt, comparator_3_lt);
  RAM #(.addrWidth(16), .dataWidth(16), .bus("separate")) ram_1 (
    .addr(ALU_out), .din(REG_rt), .data(Ram_Data), .str(Mem_WE), .clk(CLK));  // open: sel, ld, clr
  ROM #(.dataWidth(22)) rom_1 (.addr(pc_fsm_1_pc_out), .data(rom_1_data));  // open: sel
  control control_1 (
    .instruction(rom_1_data), .rt(rt), .rs(rs), .rd(rd), .imm(imm), .ALUbsrc(ALUbsrc), .ALUop(alu_op),
    .halt(halt), .Reg_WE(Reg_WE), .Display_WE(Display_WE), .Jselect(Jselect), .Branch(Branch), .jump(jump),
    .Mem_WE(Mem_WE), .RegDataSrc(RegDataSrc), .BranchOP(BranchOP));
  Multiplexer #(.width(16)) multiplexer_3 (
    .in0(REG_rt), .in1(imm), .out(multiplexer_3_out), .sel(ALUbsrc));  // open: en
  // Probe on alu_op
  Multiplexer #(.select(3), .width(16)) multiplexer_4 (
    .in0(ALU_out), .in1(imm), .in2(imm__8), .in3(REG_rs), .in4(Ram_Data), .in5(ALU_out), .in6(PC_1),
    .out(multiplexer_4_out), .sel(RegDataSrc));  // open: in7, en
  ALU alu_1 (.A(REG_rs), .B(multiplexer_3_out), .ALU_Op(alu_op), .ALU_Out(ALU_out));
  Register_File register_file_1 (
    .CLK(CLK), .rt(rt), .rs(rs), .Reg_WE(Reg_WE), .rd(rd), .REG_rd(multiplexer_4_out), .REG_rs(REG_rs),
    .REG_rt(REG_rt));
  Display display_1 (
    .Data(REG_rs), .WE(Display_WE), .CLK(CLK), .Digit0(display_1_digit0), .Digit1(display_1_digit1),
    .Digit2(display_1_digit2), .Digit3(display_1_digit3));
  Hex_Digit_Display hex_digit_display_1 (.value(display_1_digit2));  // open: dp
  Hex_Digit_Display hex_digit_display_2 (.value(display_1_digit3));  // open: dp
  LED u_halt (.in(halt));
  Hex_Digit_Display hex_digit_display_3 (.value(display_1_digit1));  // open: dp
  Hex_Digit_Display hex_digit_display_4 (.value(display_1_digit0));  // open: dp
endmodule

module Display (
  input  [15:0] Data,
  input  WE,
  input  CLK,
  output [3:0] Digit0,
  output [3:0] Digit1,
  output [3:0] Digit2,
  output [3:0] Digit3
);

  Register #(.width(16)) register_1 (.D(Data), .en(WE), .Q({Digit3, Digit2, Digit1, Digit0}), .clk(CLK));  // open: clr
endmodule

module ALU (
  input  [15:0] A,
  input  [15:0] B,
  input  [2:0] ALU_Op,
  output [15:0] ALU_Out
);

  wire [3:0] bit_extender_1_out, bit_extender_2_out;
  wire [15:0] adder_1_out, and_1_out, not_1_out, or_1_out, shifter_1_out, shifter_2_out, subtractor_1_out,
       undriven, xor_1_out;

  Subtractor #(.width(16)) subtractor_1 (.a(A), .b(B), .out(subtractor_1_out));  // open: bin, bout
  assign and_1_out = A & B & undriven;  // AND_Gate and_1, 16 bits wide
  assign or_1_out = B | undriven | A | B;  // OR_Gate or_1, 16 bits wide
  Bit_Extender #(.in_width(16), .out_width(4)) bit_extender_1 (.in(B), .out(bit_extender_1_out));
  Bit_Extender #(.in_width(16), .out_width(4)) bit_extender_2 (.in(B), .out(bit_extender_2_out));
  Adder #(.width(16)) adder_1 (.a(A), .b(B), .out(adder_1_out));  // open: cin, cout
  assign xor_1_out = A ^ B;  // XOR_Gate xor_1, 16 bits wide
  // NOT_Gate not_1 has open pins: in=open, out=not_1_out
  Shifter #(.width(16)) shifter_1 (.in(A), .\dist (bit_extender_1_out), .out(shifter_1_out));
  Shifter #(.width(16), .shift("lr")) shifter_2 (.in(A), .\dist (bit_extender_2_out), .out(shifter_2_out));
  Multiplexer #(.select(3), .width(16)) multiplexer_1 (
    .in0(adder_1_out), .in1(subtractor_1_out), .in2(and_1_out), .in3(or_1_out), .in4(xor_1_out),
    .in5(not_1_out), .in6(shifter_1_out), .in7(shifter_2_out), .out(ALU_Out), .sel(ALU_Op));  // open: en

  // Other names for the same wires on the sheet: ALU_A[15:0] = A; ALU_B[15:0] = B
endmodule

module Register_File (
  input  CLK,
  input  [2:0] rt,
  input  [2:0] rs,
  input  Reg_WE,
  input  [2:0] rd,
  input  [15:0] REG_rd,
  output [15:0] REG_rs,
  output [15:0] REG_rt
);

  wire demultiplexer_1_out1, demultiplexer_1_out2, demultiplexer_1_out3, demultiplexer_1_out4,
       demultiplexer_1_out5, demultiplexer_1_out6, demultiplexer_1_out7;
  wire [15:0] register_1_q, register_2_q, register_3_q, register_4_q, register_5_q, register_6_q,
       register_7_q;

  Demultiplexer #(.select(3)) demultiplexer_1 (
    .out1(demultiplexer_1_out1), .out2(demultiplexer_1_out2), .out3(demultiplexer_1_out3),
    .out4(demultiplexer_1_out4), .out5(demultiplexer_1_out5), .out6(demultiplexer_1_out6),
    .out7(demultiplexer_1_out7), .in(Reg_WE), .sel(rd));  // open: out0, en
  Register #(.width(16)) register_1 (.D(REG_rd), .en(demultiplexer_1_out1), .Q(register_1_q), .clk(CLK));  // open: clr
  Register #(.width(16)) register_2 (.D(REG_rd), .en(demultiplexer_1_out2), .Q(register_2_q), .clk(CLK));  // open: clr
  Register #(.width(16)) register_3 (.D(REG_rd), .en(demultiplexer_1_out3), .Q(register_3_q), .clk(CLK));  // open: clr
  Register #(.width(16)) register_4 (.D(REG_rd), .en(demultiplexer_1_out4), .Q(register_4_q), .clk(CLK));  // open: clr
  Register #(.width(16)) register_5 (.D(REG_rd), .en(demultiplexer_1_out5), .Q(register_5_q), .clk(CLK));  // open: clr
  Register #(.width(16)) register_6 (.D(REG_rd), .en(demultiplexer_1_out6), .Q(register_6_q), .clk(CLK));  // open: clr
  Register #(.width(16)) register_7 (.D(REG_rd), .en(demultiplexer_1_out7), .Q(register_7_q), .clk(CLK));  // open: clr
  Multiplexer #(.select(3), .width(16)) multiplexer_1 (
    .in0({16{1'b0}}), .in1(register_1_q), .in2(register_2_q), .in3(register_3_q), .in4(register_4_q),
    .in5(register_5_q), .in6(register_6_q), .in7(register_7_q), .out(REG_rs), .sel(rs));  // open: en
  Multiplexer #(.select(3), .width(16)) multiplexer_2 (
    .in0({16{1'b0}}), .in1(register_1_q), .in2(register_2_q), .in3(register_3_q), .in4(register_4_q),
    .in5(register_5_q), .in6(register_6_q), .in7(register_7_q), .out(REG_rt), .sel(rt));  // open: en
endmodule

module PC_FSM (
  input  CLK,
  input  [15:0] offset,
  input  [15:0] target,
  input  Jump,
  input  Branch,
  input  Halt,
  output [7:0] PC_Out,
  output [15:0] PC_1_Out
);

  wire not_1_out;
  wire [7:0] adder_1_out, bit_extender_1_out, bit_extender_2_out, multiplexer_1_out, multiplexer_2_out;

  Multiplexer #(.width(8)) multiplexer_1 (
    .in0(8'h1), .in1(bit_extender_1_out), .out(multiplexer_1_out), .sel(Branch));  // open: en
  Bit_Extender #(.in_width(16), .out_width(8)) bit_extender_1 (.in(offset), .out(bit_extender_1_out));
  Adder adder_1 (.a(PC_Out), .b(multiplexer_1_out), .out(adder_1_out));  // open: cin, cout
  Bit_Extender #(.in_width(16), .out_width(8)) bit_extender_2 (.in(target), .out(bit_extender_2_out));
  Multiplexer #(.width(8)) multiplexer_2 (
    .in0(adder_1_out), .in1(bit_extender_2_out), .out(multiplexer_2_out), .sel(Jump));  // open: en
  assign PC_1_Out = {{8{1'b0}}, adder_1_out};  // Bit_Extender bit_extender_3
  // NOT_Gate not_1 has open pins: in=open, out=not_1_out
  Register register_1 (.D(multiplexer_2_out), .en(not_1_out), .Q(PC_Out), .clk(CLK));  // open: clr
endmodule

module control (
  input  [21:0] instruction,
  output [2:0] rt,
  output [2:0] rs,
  output [2:0] rd,
  output [15:0] imm,
  output ALUbsrc,
  output [2:0] ALUop,
  output halt,
  output Reg_WE,
  output Display_WE,
  output Jselect,
  output Branch,
  output jump,
  output Mem_WE,
  output [2:0] RegDataSrc,
  output [1:0] BranchOP
);

  wire add, adi, \and , ani, beq, bge, blt, bne, j_imm, jal, jr, ld_rd, li_rd__imm, lui_rd__imm, mov_rd__rs,
       \not , \or , or_1_out, or_5_out, or_6_out, or_7_out, or_9_p4, or_10_out, or_11_out, ori, sbi, shl,
       shr, sli, sri, sub, \xor , xri;
  wire [15:0] bit_extender_1_out, bit_extender_2_out;

  Priority_Encoder priority_encoder_1 (
    .in0(1'b1), .in1(li_rd__imm), .in2(lui_rd__imm), .in3(mov_rd__rs), .in4(ld_rd), .in6(jal),
    .out(RegDataSrc));  // open: in5, in7, en_in, gs, en_out
  Decoder #(.select(5)) decoder_1 (
    .out0(halt), .out1(Display_WE), .out2(li_rd__imm), .out3(lui_rd__imm), .out4(mov_rd__rs), .out5(ld_rd),
    .out6(Mem_WE), .out7(add), .out8(sub), .out9(\and ), .out10(\or ), .out11(\xor ), .out12(\not ),
    .out13(shl), .out14(shr), .out15(adi), .out16(sbi), .out17(ani), .out18(ori), .out19(xri), .out20(sli),
    .out21(sri), .out22(j_imm), .out23(blt), .out24(bge), .out25(beq), .out26(bne), .out27(jal), .out28(jr),
    .sel(instruction[21:17]));  // open: out29, out30, out31, en
  assign bit_extender_1_out = {{8{1'b0}}, instruction[16:9]};  // Bit_Extender bit_extender_1
  assign bit_extender_2_out = {{8{instruction[16]}}, instruction[16:9]};  // Bit_Extender bit_extender_2
  Multiplexer #(.width(16)) multiplexer_1 (
    .in0(bit_extender_2_out), .in1(bit_extender_1_out), .out(imm), .sel(or_1_out));  // open: en
  or or_1 (or_1_out, li_rd__imm, ani, ori, xri);
  or or_2 (Reg_WE, li_rd__imm, lui_rd__imm, mov_rd__rs, ld_rd, add, sub, \and , \or , \xor , \not , shl, shr, adi, sbi, ani, ori, xri, sli, sri, jal);
  or or_3 (Jselect, jal, j_imm);
  or or_4 (jump, jr, jal, j_imm);
  or or_5 (or_5_out, sub, sbi);
  or or_6 (or_6_out, \and , ani);
  or or_7 (or_7_out, \xor , xri);
  or or_8 (ALUbsrc, ld_rd, adi, Mem_WE, xri, ori, ani, sli, sri, sbi);
  // OR_Gate or_9: pin names not known; wires that end beside it: \or , ori, or_7_out, or_9_p4
  or or_10 (or_10_out, shr, sri);
  or or_11 (or_11_out, shl, sli);
  Priority_Encoder priority_encoder_2 (
    .in0(1'b1), .in1(or_5_out), .in2(or_6_out), .in3(or_9_p4), .in4(or_7_out), .in5(\not ), .in6(or_11_out),
    .in7(or_10_out), .out(ALUop));  // open: en_in, gs, en_out
  or or_12 (Branch, bge, beq, bne, blt);
  Priority_Encoder #(.select(2)) priority_encoder_3 (
    .in0(1'b1), .in1(bge), .in2(beq), .in3(bne), .out(BranchOP));  // open: gs, en_out, en_in

  assign rd = instruction[8:6];
  assign rs = instruction[5:3];
  assign rt = instruction[2:0];

  // Other names for the same wires on the sheet: hlt = halt; imm8[7:0] = instruction[16:9]; put_rs = Display_WE;
  //   st__rs_imm = Mem_WE
endmodule
