// Logisim project lel112_lab5.circ as structural Verilog: 1 circuit, main circuit main
module main (
  input  [3:0] A,
  input  [3:0] B,
  input  sub
);

  wire and_1_out, and_2_out, Co, not_1_out, not_3_out, not_4_out, SOV, UOV;
  wire [3:0] MO, not_2_p2, O;

  // Probe on A
  // Probe on B
  // Probe on O
  LED led_1 (.in(UOV));
  ExactlyOne xor_1 (.out(UOV), .in1(sub), .in3(Co), .in4(Co));
  // NOT_Gate not_1 has open pins: in=open, out=not_1_out
  // NOT_Gate #(.width(4)) not_2: pin names not known; wires that end beside it: B, not_2_p2
  // Probe on A
  // Probe on B
  // Probe on O
  LED led_2 (.in(SOV));
  and and_1 (and_1_out, MO[3], A[3], not_1_out);
  Multiplexer #(.width(4)) multiplexer_1 (.in0(B), .in1(not_2_p2), .out(MO), .sel(sub));  // open: en
  not not_3 (not_3_out, A[3]);
  and and_2 (and_2_out, not_3_out, not_4_out, O[3]);
  not not_4 (not_4_out, MO[3]);
  Adder #(.width(4)) adder_1 (.a(A), .b(MO), .out(O), .cin(sub), .cout(Co));
  // OR_Gate or_1: pin names not known; wires that end beside it: and_2_out, and_1_out, SOV
endmodule
