// Logisim project lel112_lab8.circ as structural Verilog: 3 circuits, main circuit main
module main (
  input  [7:0] ALU_A,
  input  [7:0] ALU_B,
  input  [2:0] ALU_Op,
  input  [7:0] REG_rd,
  input  [2:0] rd,
  input  Reg_WE,
  input  [2:0] rs,
  input  [2:0] rt
);

  wire CLK, clock_1_out, tick_out;
  wire [7:0] ALU_Out, REG_rs, REG_rt;

  Clock clock_1 (.out(clock_1_out));
  or or_1 (CLK, clock_1_out, tick_out);
  Button tick (.out(tick_out));
  // Probe on ALU_A
  // Probe on ALU_B
  // Probe on ALU_Out
  // Probe on REG_rd
  // Probe on REG_rs
  // Probe on REG_rt
  ALU alu_1 (.A(ALU_A), .B(ALU_B), .ALU_Op(ALU_Op), .ALU_Out(ALU_Out));
  Register_File register_file_1 (
    .Reg_WE(Reg_WE), .REG_rd(REG_rd), .rs(rs), .rt(rt), .rd(rd), .REG_rs(REG_rs), .REG_rt(REG_rt));
endmodule

module ALU (
  input  [7:0] A,
  input  [7:0] B,
  input  [2:0] ALU_Op,
  output [7:0] ALU_Out
);

  wire [2:0] bit_extender_1_out, bit_extender_2_out;
  wire [7:0] adder_1_out, and_1_out, not_1_out, or_1_out, shifter_1_out, shifter_2_out, subtractor_1_out,
       undriven, xor_1_out;

  Bit_Extender #(.out_width(3)) bit_extender_1 (.in(B), .out(bit_extender_1_out));
  Adder adder_1 (.a(A), .b(B), .out(adder_1_out));  // open: cin, cout
  Subtractor subtractor_1 (.a(A), .b(B), .out(subtractor_1_out));  // open: bin, bout
  assign and_1_out = A & B & undriven;  // AND_Gate and_1, 8 bits wide
  assign or_1_out = B | undriven | A | B;  // OR_Gate or_1, 8 bits wide
  assign xor_1_out = A ^ B;  // XOR_Gate xor_1, 8 bits wide
  Shifter shifter_1 (.in(A), .\dist (bit_extender_1_out), .out(shifter_1_out));
  // NOT_Gate not_1 has open pins: in=open, out=not_1_out
  Shifter #(.shift("lr")) shifter_2 (.in(A), .\dist (bit_extender_2_out), .out(shifter_2_out));
  Bit_Extender #(.out_width(3)) bit_extender_2 (.in(B), .out(bit_extender_2_out));
  Multiplexer #(.select(3), .width(8)) multiplexer_1 (
    .in0(adder_1_out), .in1(subtractor_1_out), .in2(and_1_out), .in3(or_1_out), .in4(xor_1_out),
    .in5(not_1_out), .in6(shifter_1_out), .in7(shifter_2_out), .out(ALU_Out), .sel(ALU_Op));  // open: en
endmodule

module Register_File (
  input  Reg_WE,
  input  [7:0] REG_rd,
  input  [2:0] rs,
  input  [2:0] rt,
  input  [2:0] rd,
  output [7:0] REG_rs,
  output [7:0] REG_rt
);

  wire CLK, demultiplexer_1_out1, demultiplexer_1_out2, demultiplexer_1_out3, demultiplexer_1_out4,
       demultiplexer_1_out5, demultiplexer_1_out6, demultiplexer_1_out7;
  wire [7:0] register_2_q, register_3_q, register_4_q, register_5_q, register_6_q, register_7_q;

  Demultiplexer #(.select(3)) demultiplexer_1 (
    .out1(demultiplexer_1_out1), .out2(demultiplexer_1_out2), .out3(demultiplexer_1_out3),
    .out4(demultiplexer_1_out4), .out5(demultiplexer_1_out5), .out6(demultiplexer_1_out6),
    .out7(demultiplexer_1_out7), .in(Reg_WE), .sel(rd));  // open: out0, en
  Clock clock_1 (.out(CLK));
  Register register_1 ();  // open: D, en, Q, clk, clr
  Register register_2 (.D(REG_rd), .en(demultiplexer_1_out1), .Q(register_2_q), .clk(CLK));  // open: clr
  Register register_3 (.D(REG_rd), .en(demultiplexer_1_out2), .Q(register_3_q), .clk(CLK));  // open: clr
  Register register_4 (.D(REG_rd), .en(demultiplexer_1_out3), .Q(register_4_q), .clk(CLK));  // open: clr
  Register register_5 (.D(REG_rd), .en(demultiplexer_1_out4), .Q(register_5_q), .clk(CLK));  // open: clr
  Register register_6 (.D(REG_rd), .en(demultiplexer_1_out5), .Q(register_6_q), .clk(CLK));  // open: clr
  Register register_7 (.D(REG_rd), .en(demultiplexer_1_out6), .Q(register_7_q), .clk(CLK));  // open: clr
  Register register_8 (.D(REG_rd), .en(demultiplexer_1_out7), .Q(register_7_q), .clk(CLK));  // open: clr
  Multiplexer #(.select(3), .width(8)) multiplexer_1 (
    .in1(register_2_q), .in2(register_3_q), .in3(register_4_q), .in4(register_5_q), .in5(register_6_q),
    .in6(register_7_q), .in7(register_7_q), .out(REG_rs), .sel(rs));  // open: in0, en
  Multiplexer #(.select(3), .width(8)) multiplexer_2 (
    .in1(register_2_q), .in2(register_3_q), .in3(register_4_q), .in4(register_5_q), .in5(register_6_q),
    .in6(register_7_q), .in7(register_7_q), .out(REG_rt), .sel(rt));  // open: in0, en

  // Other names for the same wires on the sheet: WE = Reg_WE
endmodule
